# Fritzing sketch esp_flight_controller_v0_1 (saved by Fritzing 0.9.4)
perfboards: 1

parts:
  MPU9250_MPU-1 = SparkFun IMU Breakout - MPU-9250 [part_number=" SEN-13762"]  # not connected
  J1 = male pin header, 3 pins [form="♂ (male)"]
  J2 = male pin header, 3 pins [form="♂ (male)"]
  J3 = male pin header, 3 pins [form="♂ (male)"]
  J4 = male pin header, 3 pins [form="♂ (male)"]
  U1 = ESP32-38PinWide [part_number=ESP32-38PinWide]

nets:
  N1: J1.pin2, J2.pin2, J3.pin2, J4.pin2, U1.VIN
  N2: J1.pin3, J2.pin3, J3.pin3, J4.pin3, U1.GPIO11

notes:
  ESC Pins

custom parts:
  ESP32-38PinWide: Generic 38-Pin ESP32 with wide format (only access to one side of pins on a breadboard) based on Stephen Lilley's HiLetgo ESP-WROOM-32 ESP32 ESP-32S Development Board.
